# Fritzing sketch button_pull_down (saved by Fritzing 0.9.4)
breadboards: 1

parts:
  Raspberry_Pi_1 = Raspberry Pi 3 [part_number=RPI-3-V1.2]
  S1 = Pushbutton [package="[THT]"]
  R1 = Resistor [tolerance=±5% resistance=220 package=THT]

nets:
  3V3: Raspberry_Pi_1.3v3, Raspberry_Pi_1.3V3, S1.Pin_4
  N1: Raspberry_Pi_1.GPIO26, S1.Pin_2, R1.Pin_0
  N2: Raspberry_Pi_1.GND, R1.Pin_1
