# Fritzing sketch photocell_pull_down (saved by Fritzing 0.9.4)
breadboards: 1

parts:
  Raspberry_Pi_1 = Raspberry Pi 3 [part_number=RPI-3-V1.2]
  R2 = Photocell (LDR) [package=THT]
  R1 = Resistor [tolerance=±5% resistance=220 package=THT]

nets:
  N1: Raspberry_Pi_1.3v3, R2.pin_0
  N2: Raspberry_Pi_1.GPIO26, R2.pin_1, R1.Pin_0
  N3: Raspberry_Pi_1.GND, R1.Pin_1
